// Logisim project PROJETO CIRCUITOS DIGITAIS 2.0.circ as structural Verilog
module led_a (
  input  S3,
  input  S2,
  input  S1,
  input  S0,
  output out_5
);

  wire and_1_out, and_2_out, and_3_out, and_4_out, and_5_out, and_6_out, and_7_out;

  and and_1 (and_1_out, S1, ~S0);  // AND_Gate
  and and_2 (and_2_out, ~S3, S1);  // AND_Gate
  and and_3 (and_3_out, S3, ~S0);  // AND_Gate
  and and_4 (and_4_out, S3, ~S2, ~S1);  // AND_Gate
  and and_5 (and_5_out, ~S2, ~S1, ~S0);  // AND_Gate
  and and_6 (and_6_out, ~S3, S2, S0);  // AND_Gate
  and and_7 (and_7_out, S3, S2, S1);
  or or_1 (out_5, and_1_out, and_2_out, and_3_out, and_4_out, and_5_out, and_6_out, and_7_out);
endmodule

module led_b (
  input  S3,
  input  S2,
  input  S1,
  input  S0,
  output out_5
);

  wire and_1_out, and_2_out, and_3_out, and_4_out, and_5_out, and_6_out;

  and and_1 (and_1_out, ~S3, ~S2);  // AND_Gate
  and and_2 (and_2_out, ~S2, ~S1);  // AND_Gate
  and and_3 (and_3_out, ~S3, ~S1, ~S0);  // AND_Gate
  and and_4 (and_4_out, S3, ~S1, S0);  // AND_Gate
  and and_5 (and_5_out, ~S3, S1, S0);  // AND_Gate
  and and_6 (and_6_out, ~S2, ~S0);  // AND_Gate
  or or_1 (out_5, and_1_out, and_2_out, and_3_out, and_4_out, and_5_out, and_6_out);
endmodule

module led_c (
  input  S3,
  input  S2,
  input  S1,
  input  S0,
  output out_5
);

  wire and_1_out, and_2_out, and_3_out, and_4_out, and_5_out;

  and and_1 (and_1_out, S3, ~S2);  // AND_Gate
  and and_2 (and_2_out, ~S3, S2);  // AND_Gate
  and and_3 (and_3_out, ~S1, S0);  // AND_Gate
  and and_4 (and_4_out, ~S3, ~S1, ~S0);  // AND_Gate
  and and_5 (and_5_out, ~S3, S1, S0);  // AND_Gate
  or or_1 (out_5, and_1_out, and_2_out, and_3_out, and_4_out, and_5_out);
endmodule

module led_d (
  input  S3,
  input  S2,
  input  S1,
  input  S0,
  output out_5
);

  wire and_1_out, and_2_out, and_3_out, and_4_out, and_5_out;

  and and_1 (and_1_out, ~S2, S1, S0);  // AND_Gate
  and and_2 (and_2_out, ~S3, S1, ~S0);  // AND_Gate
  and and_3 (and_3_out, S2, ~S1, S0);  // AND_Gate
  and and_4 (and_4_out, S3, S2, ~S0);  // AND_Gate
  and and_5 (and_5_out, ~S2, ~S1, ~S0);  // AND_Gate
  or or_1 (out_5, and_1_out, and_2_out, and_3_out, and_4_out, and_5_out);
endmodule

module led_e (
  input  S3,
  input  S2,
  input  S1,
  input  S0,
  output out_5
);

  wire and_1_out, and_2_out, and_3_out, and_4_out;

  and and_1 (and_1_out, S3, S2);
  and and_2 (and_2_out, S1, ~S0);  // AND_Gate
  and and_3 (and_3_out, ~S2, ~S1, ~S0);  // AND_Gate
  and and_4 (and_4_out, S3, S1, S0);
  or or_1 (out_5, and_1_out, and_2_out, and_3_out, and_4_out);
endmodule

module led_f (
  input  S3,
  input  S2,
  input  S1,
  input  S0,
  output out_5
);

  wire and_1_out, and_2_out, and_3_out, and_4_out, and_5_out;

  and and_1 (and_1_out, S3, ~S2);  // AND_Gate
  and and_2 (and_2_out, ~S1, ~S0);  // AND_Gate
  and and_3 (and_3_out, S2, S1, ~S0);  // AND_Gate
  and and_4 (and_4_out, S3, S1, S0);
  and and_5 (and_5_out, ~S3, S2, ~S1);  // AND_Gate
  or or_1 (out_5, and_1_out, and_2_out, and_3_out, and_4_out, and_5_out);
endmodule

module led_g (
  input  S3,
  input  S2,
  input  S1,
  input  S0,
  output out_5
);

  wire and_1_out, and_2_out, and_3_out, and_4_out, and_5_out;

  and and_1 (and_1_out, S1, ~S0);  // AND_Gate
  and and_2 (and_2_out, S3, ~S2);  // AND_Gate
  and and_3 (and_3_out, ~S3, S2, ~S1);  // AND_Gate
  and and_4 (and_4_out, S3, S2, S0);
  and and_5 (and_5_out, ~S2, S1, S0);  // AND_Gate
  or or_1 (out_5, and_1_out, and_2_out, and_3_out, and_4_out, and_5_out);
endmodule
